# Fritzing sketch led y boton con esp32cam (saved by Fritzing 0.9.3b)
breadboards: 1

parts:
  E1 = ESP32-Cam
  LED1 = LED - 5mm [color="Red (633nm)" package="5 mm [THT]"]
  S1 = Pushbutton [package="[THT]"]
  Componente1 = FTDI Basic Programmer

nets:
  N1: E1.5V, Componente1.POWER
  N2: E1.GND#1, LED1.cathode, S1.Pin_3, S1.Pin_4, Componente1.GND
  N3: E1.GPIO_12, S1.Pin_1, S1.Pin_2
  N4: E1.GPIO_13, LED1.anode
  N5: E1.GPIO_16, Componente1.DTR
  N6: E1.GPIO_0, Componente1.RXI
  N7: E1.VCC, E1.TX/GPIO_3
